// Logisim project data3.circ as structural Verilog: 22 circuits, main circuit ◆海明传输测试1
module \国标转区位码  (
  input  [15:0] GB2312,
  output [6:0] \区号 ,
  output [6:0] \位号 
);

  wire [15:7] adder_1_out;

  // Probe on GB2312
  // Probe on \区号 
  Adder #(.width(16)) adder_1 (
    .a(GB2312), .b(16'hdfe0), .out({adder_1_out[15], \区号 , adder_1_out[7], \位号 }));  // open: cin, cout
  // Probe on \位号 

  // Notes on the sheet:
  //   请勿增改引脚，请勿修改子电路封装
  //   输入引脚区
  //   请在下方利用上方输入输出引脚的隧道标签信号构建电路，ctrl+d复制选择组件
  //   华中科技大学计算机学院 计算机组成原理课程组
  //   要求用加法器完成
  //   推荐用最新的logisim意大利hust改良版完成实验，EDU平台采用该版本进行测试
  //   输出引脚区
  //   探测区
endmodule

module \汉字显示  (
  output [15:0] EduCoder
);

  wire \时钟_out ;
  wire [6:0] \国标转区位码_1_位号 , \国标转区位码_1_区号 ;
  wire [7:0] counter_1_q;
  wire [31:0] undriven, undriven_2, undriven_3, undriven_4, undriven_5, undriven_6, undriven_7, undriven_8,
       undriven_9, undriven_10, undriven_11, undriven_12, undriven_13, undriven_14, undriven_15, undriven_16,
       undriven_17, undriven_18, undriven_19, undriven_20, undriven_21, undriven_22, undriven_23,
       undriven_24, undriven_25, undriven_26, undriven_27, undriven_28, undriven_29, undriven_30,
       undriven_31, undriven_32;

  Counter #(.width(8), .max('hff), .ongoal("wrap"), .trigger("rising"), .behavior("old")) counter_1 (
    .Q(counter_1_q), .clk(\时钟_out ));  // open: load, D, count, carry, clr, preset
  Clock #(.highDuration(1), .lowDuration(1)) \u_时钟  (.out(\时钟_out ));
  ROM #(.addrWidth(8), .dataWidth(16), .Select("high")) rom_1 (.addr(counter_1_q), .data(EduCoder));
  \国标转区位码  \u_国标转区位码_1  (.\位号 (\国标转区位码_1_位号 ), .\区号 (\国标转区位码_1_区号 ), .GB2312(EduCoder));
  DotMatrix #(.inputtype("row"), .matrixcols(32), .matrixrows(32), .persist(0), .dotshape("circle")) dotmatrix_1 (
    .row0(undriven), .row1(undriven_2), .row2(undriven_3), .row3(undriven_4), .row4(undriven_5),
    .row5(undriven_6), .row6(undriven_7), .row7(undriven_8), .row8(undriven_9), .row9(undriven_10),
    .row10(undriven_11), .row11(undriven_12), .row12(undriven_13), .row13(undriven_14), .row14(undriven_15),
    .row15(undriven_16), .row16(undriven_17), .row17(undriven_18), .row18(undriven_19), .row19(undriven_20),
    .row20(undriven_21), .row21(undriven_22), .row22(undriven_23), .row23(undriven_24), .row24(undriven_25),
    .row25(undriven_26), .row26(undriven_27), .row27(undriven_28), .row28(undriven_29), .row29(undriven_30),
    .row30(undriven_31), .row31(undriven_32));

  // Notes on the sheet:
  //   计数器
  //   GB2312
  //   实现国标转区位码电路，使得系统每个时钟正确显示一个汉字
  //   请将下面这段文字转换成GB2312替换ROM存储器中内容
  //   contents of rom_1 (hex, n*v repeats v):
  //   a3b1 a3b2 a3b3 a3b4 a3b5 a3c1 a3c2 a3c3 a3c4 a3c5 a3c6 a3c7 a3e1 a3e2 a3e3 a3e4 a3e5 a3e6 a3e7 c7e1
  //   c7e1 b5c4 ced2 d7df c1cb a3ac d5fd c8e7 ced2 c7e1 c7e1 b5c4 c0b4 a3bb ced2 c7e1 c7e1 b5c4 d5d0 cad6
  //   a3ac d7f7 b1f0 cef7 ccec b5c4 d4c6 b2ca a1a3 c4c7 bad3 c5cf b5c4 bdf0 c1f8 a3ac cac7 cfa6 d1f4 d6d0
  //   b5c4 d0c2 c4ef a3bb b2a8 b9e2 c0ef b5c4 d1de d3b0 a3ac d4da ced2 b5c4 d0c4 cdb7 b5b4 d1fa a1a3
  //   １２３４５ＡＢＣＤＥＦＧａｂｃｄｅｆｇ轻轻的我走了，正如我轻轻的来；我轻轻的招手，作别西天的云彩。那河畔的金柳，是夕阳中的新娘；波光里的艳影，在我的心头荡漾。
endmodule

// 偶校验编码
module \偶校验编码  (
  input  [15:0] \原始数据 ,
  output [16:0] \偶校验编码 
);

  wire xor_1_out, xor_2_out, xor_3_out, xor_4_out, xor_5_out, xor_6_out, xor_7_out, xor_8_out, xor_9_out,
       xor_10_out, xor_11_out, xor_12_out, xor_13_out, xor_15_out;

  xor xor_1 (xor_1_out, \原始数据 [0], \原始数据 [1]);
  xor xor_2 (xor_2_out, \原始数据 [4], \原始数据 [5]);
  xor xor_3 (xor_3_out, \原始数据 [6], \原始数据 [7]);
  xor xor_4 (xor_4_out, \原始数据 [8], \原始数据 [9]);
  xor xor_5 (xor_5_out, \原始数据 [10], \原始数据 [11]);
  xor xor_6 (xor_6_out, \原始数据 [14], \原始数据 [15]);
  xor xor_7 (xor_7_out, xor_1_out, \原始数据 [2]);
  xor xor_8 (xor_8_out, xor_2_out, xor_3_out);
  xor xor_9 (xor_9_out, xor_4_out, xor_5_out);
  xor xor_10 (xor_10_out, \原始数据 [13], xor_6_out);
  xor xor_11 (xor_11_out, xor_7_out, \原始数据 [3]);
  xor xor_12 (xor_12_out, xor_8_out, xor_9_out);
  xor xor_13 (xor_13_out, \原始数据 [12], xor_10_out);
  xor xor_14 (\偶校验编码 [16], xor_11_out, xor_15_out);
  xor xor_15 (xor_15_out, xor_12_out, xor_13_out);

  assign \偶校验编码 [15:0] = \原始数据 ;

  // Other names for the same wires on the sheet: D1 = \原始数据 [0]; Data[15:0] = \原始数据 ;
  //   校验码[16:0] = {\偶校验编码 [16], \原始数据 }; D2 = \原始数据 [1]; D3 = \原始数据 [2]; D4 = \原始数据 [3]; D5 = \原始数据 [4];
  //   D6 = \原始数据 [5]; D7 = \原始数据 [6]; D8 = \原始数据 [7]; D9 = \原始数据 [8]; D10 = \原始数据 [9]; D11 = \原始数据 [10];
  //   D12 = \原始数据 [11]; D13 = \原始数据 [12]; D14 = \原始数据 [13]; D15 = \原始数据 [14]; D16 = \原始数据 [15]

  // Notes on the sheet:
  //   输入引脚区
  //   请勿增改引脚，请勿修改子电路封装
  //   电路功能：实现16位数据位的偶校验编码，输入：16位数据；输出：17位校验码（数据位+校验位）
  //   请在下方利用上方输入输出引脚的隧道信号构建电路，ctrl+d复制选择部件
  //   输出引脚区
endmodule

// 偶校验检错
module \偶校验检错  (
  input  [16:0] \偶校验编码 ,
  output \检错位 ,
  output [15:0] \数据位 
);

  wire xor_1_out, xor_2_out, xor_3_out, xor_4_out, xor_5_out;

  xor xor_1 (xor_1_out, \偶校验编码 [0], \偶校验编码 [1], \偶校验编码 [2], \偶校验编码 [3]);
  xor xor_2 (xor_2_out, \偶校验编码 [4], \偶校验编码 [5], \偶校验编码 [6], \偶校验编码 [7]);
  xor xor_3 (xor_3_out, \偶校验编码 [8], \偶校验编码 [9], \偶校验编码 [10], \偶校验编码 [11]);
  xor xor_4 (xor_4_out, \偶校验编码 [12], \偶校验编码 [13], \偶校验编码 [14], \偶校验编码 [15]);
  xor xor_5 (xor_5_out, xor_1_out, xor_2_out, xor_3_out, xor_4_out);
  xor xor_6 (\检错位 , xor_5_out, \偶校验编码 [16]);

  assign \数据位  = \偶校验编码 [15:0];

  // Other names for the same wires on the sheet: D1 = \偶校验编码 [0]; 偶校验码[16:0] = \偶校验编码 ; D2 = \偶校验编码 [1];
  //   D3 = \偶校验编码 [2]; D4 = \偶校验编码 [3]; D5 = \偶校验编码 [4]; D6 = \偶校验编码 [5]; D7 = \偶校验编码 [6]; D8 = \偶校验编码 [7];
  //   D9 = \偶校验编码 [8]; D10 = \偶校验编码 [9]; D11 = \偶校验编码 [10]; D12 = \偶校验编码 [11]; D13 = \偶校验编码 [12]; D14 = \偶校验编码 [13];
  //   D15 = \偶校验编码 [14]; D16 = \偶校验编码 [15]; P1 = \偶校验编码 [16]

  // Notes on the sheet:
  //   输入引脚区
  //   请勿增改引脚，请勿修改子电路封装
  //   电路功能：实现17位偶校验编码的检错以及数据提取。输入：17位校验码；输出：检错位、数据位
  //   请在下方利用上方输入输出引脚的隧道信号构建电路，ctrl+d复制选择部件
  //   输出引脚区
endmodule

// 海明编码
module \海明编码  (
  input  [15:0] \原始数据 ,
  output [21:0] \海明码 
);

  xor xor_1 (\海明码 [7], \原始数据 [10], \原始数据 [9], \原始数据 [8], \原始数据 [7], \原始数据 [6], \原始数据 [5], \原始数据 [4]);
  xor xor_2 (\海明码 [0], \原始数据 [0], \原始数据 [1], \原始数据 [3], \原始数据 [4], \原始数据 [6], \原始数据 [8], \原始数据 [10], \原始数据 [11], \原始数据 [13], \原始数据 [15]);
  xor xor_3 (\海明码 [1], \原始数据 [13], \原始数据 [12], \原始数据 [10], \原始数据 [9], \原始数据 [6], \原始数据 [5], \原始数据 [3], \原始数据 [2], \原始数据 [0]);
  xor xor_4 (\海明码 [15], \原始数据 [15], \原始数据 [14], \原始数据 [13], \原始数据 [12], \原始数据 [11]);
  xor xor_5 (\海明码 [3], \原始数据 [15], \原始数据 [14], \原始数据 [10], \原始数据 [9], \原始数据 [8], \原始数据 [7], \原始数据 [3], \原始数据 [2], \原始数据 [1]);
  xor xor_6 (\海明码 [21], \原始数据 [15], \原始数据 [14], \原始数据 [13], \原始数据 [12], \原始数据 [11], \海明码 [15], \原始数据 [10], \原始数据 [9], \原始数据 [8], \原始数据 [7], \原始数据 [6], \原始数据 [5], \原始数据 [4], \海明码 [7], \原始数据 [3], \原始数据 [2], \原始数据 [1], \海明码 [3], \原始数据 [0], \海明码 [1], \海明码 [0]);

  assign {\海明码 [20:16], \海明码 [14:8], \海明码 [6:4], \海明码 [2]} = \原始数据 ;

  // Other names for the same wires on the sheet: P1 = \海明码 [0]; P2 = \海明码 [1]; D1 = \原始数据 [0]; Data[15:0] = \原始数据 ;
  //   P3 = \海明码 [3]; D2 = \原始数据 [1]; D3 = \原始数据 [2]; D4 = \原始数据 [3]; P4 = \海明码 [7]; D5 = \原始数据 [4]; D6 = \原始数据 [5];
  //   D7 = \原始数据 [6]; D8 = \原始数据 [7]; D9 = \原始数据 [8]; D10 = \原始数据 [9]; D11 = \原始数据 [10]; P5 = \海明码 [15];
  //   D12 = \原始数据 [11]; D13 = \原始数据 [12]; D14 = \原始数据 [13]; D15 = \原始数据 [14]; D16 = \原始数据 [15]; P6 = \海明码 [21]

  // Notes on the sheet:
  //   输入引脚区
  //   请勿增改引脚，请勿修改子电路封装
  //   电路功能：海明编码电路，可检两位错并纠一位错，输入：16位；输出：22位海明码（数据位+校验位）
  //   请在下方利用上方输入输出引脚的隧道信号构建电路，ctrl+d复制选择部件
  //   输出引脚区
  //   注意异或门需要设置多输入行为：奇数个1时输出为1，否则功能不正确
endmodule

// 海明解码
module \海明解码  (
  input  [21:0] \海明码 ,
  output \_0位错 ,
  output \_1位错 ,
  output \_2位错 ,
  output [15:0] \纠错后数据 
);


  // Other names for the same wires on the sheet: P1 = \海明码 [0]; P2 = \海明码 [1]; D1 = \海明码 [2]; P3 = \海明码 [3];
  //   D2 = \海明码 [4]; D3 = \海明码 [5]; D4 = \海明码 [6]; P4 = \海明码 [7]; D5 = \海明码 [8]; D6 = \海明码 [9]; D7 = \海明码 [10];
  //   D8 = \海明码 [11]; D9 = \海明码 [12]; D10 = \海明码 [13]; D11 = \海明码 [14]; P5 = \海明码 [15]; D12 = \海明码 [16];
  //   D13 = \海明码 [17]; D14 = \海明码 [18]; D15 = \海明码 [19]; D16 = \海明码 [20]; P6 = \海明码 [21]

  // Notes on the sheet:
  //   输入引脚区
  //   输出引脚区
  //   注意异或门需要设置多输入行为：奇数个1时输出为1，否则功能不正确
  //   电路功能：
  //   请勿增改引脚，请勿修改子电路封装
  //   输入：22位海明码；输出：纠错后的数据、错误模式
  //   请在下方利用上方输入输出引脚的隧道信号构建电路，ctrl+d复制选择部件
  //   实现22位海明码的数据解码，能判断1位错，2位错，无错误，1位错自动纠错。
  //   总偶校验检错位
endmodule

// CRC编码
module \CRC编码  (
  input  [15:0] \原始数据 ,
  output [21:0] \CRC校验码 
);


  // Other names for the same wires on the sheet: D1 = \原始数据 [0]; Data[15:0] = \原始数据 ; D2 = \原始数据 [1]; D3 = \原始数据 [2];
  //   D4 = \原始数据 [3]; D5 = \原始数据 [4]; D6 = \原始数据 [5]; D7 = \原始数据 [6]; D9 = \原始数据 [8]; CRC编码[21:0] = \CRC校验码 ;
  //   D8 = \原始数据 [7]; D10 = \原始数据 [9]; D11 = \原始数据 [10]; D12 = \原始数据 [11]; D13 = \原始数据 [12]; D14 = \原始数据 [13];
  //   D15 = \原始数据 [14]; D16 = \原始数据 [15]

  // Notes on the sheet:
  //   输入引脚区
  //   请勿增改引脚，请勿修改子电路封装
  //   注意异或门需要设置多输入行为：奇数个1时输出为1，否则功能不正确
  //   电路功能：CRC编码电路，可检两位错并纠一位错，输入：16位；输出：22位海明码（数据位+校验位）
  //   请在下方利用上方输入输出引脚的隧道信号构建电路，ctrl+d复制选择部件
  //   输出引脚区
endmodule

// CRC解码
module \CRC解码  (
  input  [21:0] \CRC编码 ,
  output \_0位错 ,
  output \_1位错 ,
  output \_2位错 ,
  output [15:0] \纠错后数据 
);


  // Other names for the same wires on the sheet: CRC[21:0] = \CRC编码 ; r1 = \CRC编码 [0]; r2 = \CRC编码 [1];
  //   r3 = \CRC编码 [2]; r4 = \CRC编码 [3]; r5 = \CRC编码 [4]; r6 = \CRC编码 [5]; D1 = \CRC编码 [6]; D2 = \CRC编码 [7];
  //   D3 = \CRC编码 [8]; D4 = \CRC编码 [9]; D5 = \CRC编码 [10]; D6 = \CRC编码 [11]; D7 = \CRC编码 [12]; D8 = \CRC编码 [13];
  //   D9 = \CRC编码 [14]; D10 = \CRC编码 [15]; D11 = \CRC编码 [16]; D12 = \CRC编码 [17]; D13 = \CRC编码 [18]; D14 = \CRC编码 [19];
  //   D15 = \CRC编码 [20]; D16 = \CRC编码 [21]

  // Notes on the sheet:
  //   输入引脚区
  //   输出引脚区
  //   注意异或门需要设置多输入行为：奇数个1时输出为1，否则功能不正确
  //   电路功能：
  //   请勿增改引脚，请勿修改子电路封装
  //   输入：22位CRC编码；输出：纠错后的数据、错误模式
  //   请在下方利用上方输入输出引脚的隧道信号构建电路，ctrl+d复制选择部件
  //   实现22位海CRC编码的数据解码，能判断1位错，2位错，无错误，1位错自动纠错。
endmodule

module \偶校验传输测试  (
);

  wire and_1_out, comparator_1_eq, \偶校验检错_1_检错位 , \时钟_2_out , \时钟_out ;
  wire [6:0] \国标转区位码_1_位号 , \国标转区位码_1_区号 , \国标转区位码_2_位号 , \国标转区位码_2_区号 ;
  wire [7:0] counter_1_q;
  wire [15:0] \发送 , \接收 ;
  wire [16:0] \n17位随机干扰_1_加扰后数据 , \n17位随机干扰_1_随机加扰屏蔽字 , \偶校验编码_1_偶校验编码 ;
  wire [31:0] undriven, undriven_2, undriven_3, undriven_4, undriven_5, undriven_6, undriven_7, undriven_8,
       undriven_9, undriven_10, undriven_11, undriven_12, undriven_13, undriven_14, undriven_15, undriven_16,
       undriven_17, undriven_18, undriven_19, undriven_20, undriven_21, undriven_22, undriven_23,
       undriven_24, undriven_25, undriven_26, undriven_27, undriven_28, undriven_29, undriven_30,
       undriven_31, undriven_32, undriven_33, undriven_34, undriven_35, undriven_36, undriven_37,
       undriven_38, undriven_39, undriven_40, undriven_41, undriven_42, undriven_43, undriven_44,
       undriven_45, undriven_46, undriven_47, undriven_48, undriven_49, undriven_50, undriven_51,
       undriven_52, undriven_53, undriven_54, undriven_55, undriven_56, undriven_57, undriven_58,
       undriven_59, undriven_60, undriven_61, undriven_62, undriven_63, undriven_64;

  Counter #(.width(8), .max('hff), .ongoal("wrap"), .trigger("rising"), .behavior("old")) counter_1 (
    .Q(counter_1_q), .clk(\时钟_out ));  // open: load, D, count, carry, clr, preset
  Clock #(.highDuration(1), .lowDuration(1)) \u_时钟  (.out(\时钟_out ));
  \国标转区位码  \u_国标转区位码_1  (.\位号 (\国标转区位码_1_位号 ), .\区号 (\国标转区位码_1_区号 ), .GB2312(\发送 ));
  ROM #(.addrWidth(8), .dataWidth(16), .Select("high")) rom_1 (.addr(counter_1_q), .data(\发送 ));
  DotMatrix #(.inputtype("row"), .matrixcols(32), .matrixrows(32), .persist(0), .dotshape("circle")) dotmatrix_1 (
    .row0(undriven), .row1(undriven_2), .row2(undriven_3), .row3(undriven_4), .row4(undriven_5),
    .row5(undriven_6), .row6(undriven_7), .row7(undriven_8), .row8(undriven_9), .row9(undriven_10),
    .row10(undriven_11), .row11(undriven_12), .row12(undriven_13), .row13(undriven_14), .row14(undriven_15),
    .row15(undriven_16), .row16(undriven_17), .row17(undriven_18), .row18(undriven_19), .row19(undriven_20),
    .row20(undriven_21), .row21(undriven_22), .row22(undriven_23), .row23(undriven_24), .row24(undriven_25),
    .row25(undriven_26), .row26(undriven_27), .row27(undriven_28), .row28(undriven_29), .row29(undriven_30),
    .row30(undriven_31), .row31(undriven_32));
  // Probe on \发送 
  \偶校验编码  \u_偶校验编码_1  (.\原始数据 (\发送 ), .\偶校验编码 (\偶校验编码_1_偶校验编码 ));
  // Probe on \偶校验编码_1_偶校验编码 
  // Probe on \偶校验编码_1_偶校验编码 
  // Probe on \n17位随机干扰_1_随机加扰屏蔽字 
  \_17位随机干扰  \u_17位随机干扰_1  (
    .\_17位输入 (\偶校验编码_1_偶校验编码 ), .\随机加扰屏蔽字 (\n17位随机干扰_1_随机加扰屏蔽字 ), .\加扰后数据 (\n17位随机干扰_1_加扰后数据 ),
    .CLK(\时钟_2_out ));
  Clock #(.highDuration(1), .lowDuration(1)) \u_时钟_2  (.out(\时钟_2_out ));
  // Probe on \n17位随机干扰_1_加扰后数据 
  // Probe on \n17位随机干扰_1_加扰后数据 
  \国标转区位码  \u_国标转区位码_2  (.\位号 (\国标转区位码_2_位号 ), .\区号 (\国标转区位码_2_区号 ), .GB2312(\接收 ));
  DotMatrix #(.inputtype("row"), .matrixcols(32), .matrixrows(32), .persist(0), .dotshape("circle")) dotmatrix_2 (
    .row0(undriven_33), .row1(undriven_34), .row2(undriven_35), .row3(undriven_36), .row4(undriven_37),
    .row5(undriven_38), .row6(undriven_39), .row7(undriven_40), .row8(undriven_41), .row9(undriven_42),
    .row10(undriven_43), .row11(undriven_44), .row12(undriven_45), .row13(undriven_46), .row14(undriven_47),
    .row15(undriven_48), .row16(undriven_49), .row17(undriven_50), .row18(undriven_51), .row19(undriven_52),
    .row20(undriven_53), .row21(undriven_54), .row22(undriven_55), .row23(undriven_56), .row24(undriven_57),
    .row25(undriven_58), .row26(undriven_59), .row27(undriven_60), .row28(undriven_61), .row29(undriven_62),
    .row30(undriven_63), .row31(undriven_64));
  LED #(.active("true")) \u_检错位  (.in(\偶校验检错_1_检错位 ));
  \偶校验检错  \u_偶校验检错_1  (.\检错位 (\偶校验检错_1_检错位 ), .\偶校验编码 (\n17位随机干扰_1_加扰后数据 ), .\数据位 (\接收 ));
  Comparator #(.width(16), .mode("twosComplement")) comparator_1 (
    .a(\发送 ), .b(\接收 ), .eq(comparator_1_eq));  // open: gt, lt
  // Probe on \接收 
  and and_1 (and_1_out, ~comparator_1_eq, ~\偶校验检错_1_检错位 );  // AND_Gate
  LED #(.active("true")) \u_数据正确  (.in(comparator_1_eq));
  LED #(.active("true")) \u_误报  (.in(and_1_out));

  // Notes on the sheet:
  //   发送方
  //   计数器
  //   发送方
  //   汉字显示
  //   GB2312
  //   contents of rom_1 (hex, n*v repeats v):
  //   bbaa d6d0 bfc6 bcbc b4f3 d1a7 cac7 b9fa bcd2 bdcc d3fd b2bf d6b1 caf4 b5c4 c8ab b9fa d6d8 b5e3 b4f3
  //   d1a7 a3ac d3c9 d4ad bbaa d6d0 c0ed b9a4 b4f3 d1a7 a1a2 cdac bcc3 d2bd bfc6 b4f3 d1a7 a1a2 cee4 baba
  //   b3c7 cad0 bda8 c9e8 d1a7 d4ba d3da a3b2 a3b0 a3b0 a3b0 c4ea a3b5 d4c2 a3b2 a3b6 c8d5 bacf b2a2 b3c9
  //   c1a2 a3ac cac7 cad7 c5fa c1d0 c8eb b9fa bcd2 a1b0 a3b2 a3b1 a3b1 b9a4 b3cc a1b1 d6d8 b5e3 bda8 c9e8
  //   bacd b9fa bcd2 a1b0 a3b9 a3b8 a3b5 b9a4 b3cc a1b1 bda8 c9e8 b8df d0a3 d6ae d2bb a1a3 d1a7 d0a3 d0a3
  //   d4b0 d5bc b5d8 c6df c7a7 d3e0 c4b6 a3ac d4b0 c4da caf7 c4be b4d0 dcd7 a3ac b1cc b2dd c8e7 d2f0 a3ac
  //   bbb7 beb3 d3c5 d1c5 a3ac beb0 c9ab d0e3 c0f6 a3ac c2cc bbaf b8b2 b8c7 c2ca 3732 25a3 acb1 bbd3 fece
  //   aaa1 b0c9 adc1 d6ca bdb4 f3d1 a7a1 b1a1
  //   发送方在ROM预存了一段中文文字，通过计数器驱动电路每个时钟传输一个汉字到接收方
  //   用户实现了国标转区位码电路后，可在中间窗口观察发送方和接收方汉字显示是否一致以观察检错性能
  //   电路功能：测试偶校验编解码电路正确性，仿真时设置加扰控制位和原始数据，按CTRL+T触发不同的干扰，检验编解码电路功能
  //   偶校验编解码传输电路
  //   接收方
  //   汉字显示
  //   Ctrl+T  Ctrl+K 驱动时钟触发随机干扰变化
  //   接收方
  //   请将时钟频率调到8Hz
endmodule

module \海明传输测试1  (
  input  [15:0] \原始数据 ,
  input  [1:0] \加扰控制 
);

  wire clock_1_out, comparator_1_eq, \海明解码_1__0位错 , \海明解码_1__1位错 , \海明解码_1__2位错 ;
  wire [15:0] \海明解码_1_纠错后数据 ;
  wire [21:0] \n22位随机干扰_1_加扰后数据 , \n22位随机干扰_1_随机加扰屏蔽字 , \海明编码_1_海明码 ;

  // Probe on \原始数据 
  // Probe on \海明编码_1_海明码 
  \海明编码  \u_海明编码_1  (.\原始数据 (\原始数据 ), .\海明码 (\海明编码_1_海明码 ));
  // Probe on \海明编码_1_海明码 
  // Probe on \n22位随机干扰_1_随机加扰屏蔽字 
  Clock #(.highDuration(1), .lowDuration(1)) clock_1 (.out(clock_1_out));
  // Probe on \n22位随机干扰_1_加扰后数据 
  \_22位随机干扰  \u_22位随机干扰_1  (
    .\加扰模式 (\加扰控制 ), .\随机加扰屏蔽字 (\n22位随机干扰_1_随机加扰屏蔽字 ), .\_22位输入 (\海明编码_1_海明码 ), .\加扰后数据 (\n22位随机干扰_1_加扰后数据 ),
    .CLK(clock_1_out));  // open: 增加三位错, EDU
  // Probe on \n22位随机干扰_1_加扰后数据 
  LED #(.active("true")) \u_一位错  (.in(\海明解码_1__1位错 ));
  LED #(.active("true")) \u_两位错  (.in(\海明解码_1__2位错 ));
  LED #(.active("true")) OK (.in(\海明解码_1__0位错 ));
  \海明解码  \u_海明解码_1  (
    .\_1位错 (\海明解码_1__1位错 ), .\_2位错 (\海明解码_1__2位错 ), .\_0位错 (\海明解码_1__0位错 ), .\海明码 (\n22位随机干扰_1_加扰后数据 ),
    .\纠错后数据 (\海明解码_1_纠错后数据 ));
  // Probe on \海明解码_1_纠错后数据 
  LED #(.active("true")) \u_数据正确  (.in(comparator_1_eq));
  Comparator #(.width(16), .mode("twosComplement")) comparator_1 (
    .a(\原始数据 ), .b(\海明解码_1_纠错后数据 ), .eq(comparator_1_eq));  // open: gt, lt

  // Notes on the sheet:
  //   发送方
  //   Ctrl+T 驱动时钟触发随机干扰变化
  //   海明编解码传输电路
  //   电路功能：测试海明编解码电路正确性，仿真时设置加扰控制位和原始数据，按CTRL+T触发不同的干扰，检验编解码电路功能
  //   加扰控制00：不加扰  01:1位加扰 10:2位加扰 11：随机加扰
  //   接收方
endmodule

module \海明传输测试2  (
  input  [1:0] \加扰控制 
);

  wire CLK, comparator_1_eq, \海明解码_1__0位错 , \海明解码_1__1位错 , \海明解码_1__2位错 ;
  wire [6:0] \国标转区位码_1_位号 , \国标转区位码_1_区号 , \国标转区位码_2_位号 , \国标转区位码_2_区号 ;
  wire [7:0] counter_1_q;
  wire [15:0] \发送 , \接收 ;
  wire [21:0] \n22位随机干扰_1_加扰后数据 , \n22位随机干扰_1_随机加扰屏蔽字 , \海明编码_1_海明码 ;
  wire [31:0] undriven, undriven_2, undriven_3, undriven_4, undriven_5, undriven_6, undriven_7, undriven_8,
       undriven_9, undriven_10, undriven_11, undriven_12, undriven_13, undriven_14, undriven_15, undriven_16,
       undriven_17, undriven_18, undriven_19, undriven_20, undriven_21, undriven_22, undriven_23,
       undriven_24, undriven_25, undriven_26, undriven_27, undriven_28, undriven_29, undriven_30,
       undriven_31, undriven_32, undriven_33, undriven_34, undriven_35, undriven_36, undriven_37,
       undriven_38, undriven_39, undriven_40, undriven_41, undriven_42, undriven_43, undriven_44,
       undriven_45, undriven_46, undriven_47, undriven_48, undriven_49, undriven_50, undriven_51,
       undriven_52, undriven_53, undriven_54, undriven_55, undriven_56, undriven_57, undriven_58,
       undriven_59, undriven_60, undriven_61, undriven_62, undriven_63, undriven_64;

  Counter #(.width(8), .max('hff), .ongoal("wrap"), .trigger("rising"), .behavior("old")) counter_1 (
    .Q(counter_1_q), .clk(CLK));  // open: load, D, count, carry, clr, preset
  Clock #(.highDuration(1), .lowDuration(1)) \u_时钟  (.out(CLK));
  \国标转区位码  \u_国标转区位码_1  (.\位号 (\国标转区位码_1_位号 ), .\区号 (\国标转区位码_1_区号 ), .GB2312(\发送 ));
  DotMatrix #(.inputtype("row"), .matrixcols(32), .matrixrows(32), .persist(0), .dotshape("circle")) dotmatrix_1 (
    .row0(undriven), .row1(undriven_2), .row2(undriven_3), .row3(undriven_4), .row4(undriven_5),
    .row5(undriven_6), .row6(undriven_7), .row7(undriven_8), .row8(undriven_9), .row9(undriven_10),
    .row10(undriven_11), .row11(undriven_12), .row12(undriven_13), .row13(undriven_14), .row14(undriven_15),
    .row15(undriven_16), .row16(undriven_17), .row17(undriven_18), .row18(undriven_19), .row19(undriven_20),
    .row20(undriven_21), .row21(undriven_22), .row22(undriven_23), .row23(undriven_24), .row24(undriven_25),
    .row25(undriven_26), .row26(undriven_27), .row27(undriven_28), .row28(undriven_29), .row29(undriven_30),
    .row30(undriven_31), .row31(undriven_32));
  ROM #(.addrWidth(8), .dataWidth(16), .Select("high")) rom_1 (.addr(counter_1_q), .data(\发送 ));
  // Probe on \发送 
  // Probe on \海明编码_1_海明码 
  \海明编码  \u_海明编码_1  (.\原始数据 (\发送 ), .\海明码 (\海明编码_1_海明码 ));
  // Probe on \海明编码_1_海明码 
  // Probe on \n22位随机干扰_1_随机加扰屏蔽字 
  \_22位随机干扰  \u_22位随机干扰_1  (
    .\加扰模式 (\加扰控制 ), .\随机加扰屏蔽字 (\n22位随机干扰_1_随机加扰屏蔽字 ), .\_22位输入 (\海明编码_1_海明码 ), .\加扰后数据 (\n22位随机干扰_1_加扰后数据 ),
    .CLK(CLK));  // open: 增加三位错, EDU
  \国标转区位码  \u_国标转区位码_2  (.\位号 (\国标转区位码_2_位号 ), .\区号 (\国标转区位码_2_区号 ), .GB2312(\接收 ));
  // Probe on \n22位随机干扰_1_加扰后数据 
  // Probe on \n22位随机干扰_1_加扰后数据 
  LED #(.active("true")) \u_一位错  (.in(\海明解码_1__1位错 ));
  LED #(.active("true")) \u_两位错  (.in(\海明解码_1__2位错 ));
  LED #(.active("true")) OK (.in(\海明解码_1__0位错 ));
  DotMatrix #(.inputtype("row"), .matrixcols(32), .matrixrows(32), .persist(0), .dotshape("circle")) dotmatrix_2 (
    .row0(undriven_33), .row1(undriven_34), .row2(undriven_35), .row3(undriven_36), .row4(undriven_37),
    .row5(undriven_38), .row6(undriven_39), .row7(undriven_40), .row8(undriven_41), .row9(undriven_42),
    .row10(undriven_43), .row11(undriven_44), .row12(undriven_45), .row13(undriven_46), .row14(undriven_47),
    .row15(undriven_48), .row16(undriven_49), .row17(undriven_50), .row18(undriven_51), .row19(undriven_52),
    .row20(undriven_53), .row21(undriven_54), .row22(undriven_55), .row23(undriven_56), .row24(undriven_57),
    .row25(undriven_58), .row26(undriven_59), .row27(undriven_60), .row28(undriven_61), .row29(undriven_62),
    .row30(undriven_63), .row31(undriven_64));
  \海明解码  \u_海明解码_1  (
    .\_1位错 (\海明解码_1__1位错 ), .\_2位错 (\海明解码_1__2位错 ), .\_0位错 (\海明解码_1__0位错 ), .\海明码 (\n22位随机干扰_1_加扰后数据 ),
    .\纠错后数据 (\接收 ));
  // Probe on \接收 
  Comparator #(.width(16), .mode("twosComplement")) comparator_1 (
    .a(\发送 ), .b(\接收 ), .eq(comparator_1_eq));  // open: gt, lt
  LED #(.active("true")) \u_数据正确  (.in(comparator_1_eq));

  // Notes on the sheet:
  //   发送方
  //   计数器
  //   发送方
  //   汉字显示
  //   GB2312
  //   contents of rom_1 (hex, n*v repeats v):
  //   bbaa d6d0 bfc6 bcbc b4f3 d1a7 cac7 b9fa bcd2 bdcc d3fd b2bf d6b1 caf4 b5c4 c8ab b9fa d6d8 b5e3 b4f3
  //   d1a7 a3ac d3c9 d4ad bbaa d6d0 c0ed b9a4 b4f3 d1a7 a1a2 cdac bcc3 d2bd bfc6 b4f3 d1a7 a1a2 cee4 baba
  //   b3c7 cad0 bda8 c9e8 d1a7 d4ba d3da a3b2 a3b0 a3b0 a3b0 c4ea a3b5 d4c2 a3b2 a3b6 c8d5 bacf b2a2 b3c9
  //   c1a2 a3ac cac7 cad7 c5fa c1d0 c8eb b9fa bcd2 a1b0 a3b2 a3b1 a3b1 b9a4 b3cc a1b1 d6d8 b5e3 bda8 c9e8
  //   bacd b9fa bcd2 a1b0 a3b9 a3b8 a3b5 b9a4 b3cc a1b1 bda8 c9e8 b8df d0a3 d6ae d2bb a1a3 d1a7 d0a3 d0a3
  //   d4b0 d5bc b5d8 c6df c7a7 d3e0 c4b6 a3ac d4b0 c4da caf7 c4be b4d0 dcd7 a3ac b1cc b2dd c8e7 d2f0 a3ac
  //   bbb7 beb3 d3c5 d1c5 a3ac beb0 c9ab d0e3 c0f6 a3ac c2cc bbaf b8b2 b8c7 c2ca 3732 25a3 acb1 bbd3 fece
  //   aaa1 b0c9 adc1 d6ca bdb4 f3d1 a7a1 b1a1
  //   Ctrl+T 驱动时钟触发随机干扰变化
  //   发送方在ROM预存了一段中文文字，通过计数器驱动电路每个时钟传输一个汉字到接收方
  //   电路功能：测试海明编解码电路正确性，仿真时设置加扰控制位和原始数据，按CTRL+T触发不同的干扰，检验编解码电路功能
  //   用户实现了国标转区位码电路后，可在中间窗口观察发送方和接收方汉字显示是否一致以观察海明检错纠错性能
  //   海明编解码传输电路
  //   接收方
  //   汉字显示
  //   Ctrl+T 驱动时钟触发随机干扰变化
  //   加扰控制00：不加扰  01:1位加扰 10:2位加扰 11：随机加扰
  //   加扰控制00：不加扰  01:1位加扰 10:2位加扰 11：随机加扰
  //   接收方
  //   请将时钟频率调到8Hz
endmodule

// Hamming
module \海明编码流水传输  (
  input  \加噪 ,
  input  EDU,
  output _1err,
  output _2err,
  output clr2,
  output clr3,
  output clr4,
  output en5
);

  wire CLK, \n16位流水接口_1_传输状态out_表明当前传输数据有效 , \n22位流水接口_1_传输状态out_表明当前传输数据有效 ,
       \n22位流水接口_2_传输状态out_表明当前传输数据有效 , \海明解码_1__0位错 ;
  wire [6:0] \国标转区位码_1_位号 , \国标转区位码_1_区号 , \国标转区位码_2_位号 , \国标转区位码_2_区号 ;
  wire [7:0] adder_1_out, CNT;
  wire [15:0] \n16位流水接口_1_dout16 , \发送 , \接收 , \海明解码_1_纠错后数据 ;
  wire [21:0] \n22位流水接口_1_dout22 , \n22位流水接口_2_dout22 , \n22位随机干扰_1_加扰后数据 , \海明编码_1_海明码 ;
  wire [31:0] undriven, undriven_2, undriven_3, undriven_4, undriven_5, undriven_6, undriven_7, undriven_8,
       undriven_9, undriven_10, undriven_11, undriven_12, undriven_13, undriven_14, undriven_15, undriven_16,
       undriven_17, undriven_18, undriven_19, undriven_20, undriven_21, undriven_22, undriven_23,
       undriven_24, undriven_25, undriven_26, undriven_27, undriven_28, undriven_29, undriven_30,
       undriven_31, undriven_32, undriven_33, undriven_34, undriven_35, undriven_36, undriven_37,
       undriven_38, undriven_39, undriven_40, undriven_41, undriven_42, undriven_43, undriven_44,
       undriven_45, undriven_46, undriven_47, undriven_48, undriven_49, undriven_50, undriven_51,
       undriven_52, undriven_53, undriven_54, undriven_55, undriven_56, undriven_57, undriven_58,
       undriven_59, undriven_60, undriven_61, undriven_62, undriven_63, undriven_64;

  Register #(.width(8), .trigger("rising"), .Select("low")) register_1 (
    .D(adder_1_out), .Q(CNT), .clk(CLK));  // open: en, clr
  Clock #(.highDuration(1), .lowDuration(1)) \u_时钟  (.out(CLK));
  \国标转区位码  \u_国标转区位码_1  (.\位号 (\国标转区位码_1_位号 ), .\区号 (\国标转区位码_1_区号 ), .GB2312(\发送 ));
  Adder #(.width(8)) adder_1 (.a(8'h1), .b(CNT), .out(adder_1_out));  // open: cin, cout
  DotMatrix #(.inputtype("row"), .matrixcols(32), .matrixrows(32), .persist(0), .dotshape("circle")) dotmatrix_1 (
    .row0(undriven), .row1(undriven_2), .row2(undriven_3), .row3(undriven_4), .row4(undriven_5),
    .row5(undriven_6), .row6(undriven_7), .row7(undriven_8), .row8(undriven_9), .row9(undriven_10),
    .row10(undriven_11), .row11(undriven_12), .row12(undriven_13), .row13(undriven_14), .row14(undriven_15),
    .row15(undriven_16), .row16(undriven_17), .row17(undriven_18), .row18(undriven_19), .row19(undriven_20),
    .row20(undriven_21), .row21(undriven_22), .row22(undriven_23), .row23(undriven_24), .row24(undriven_25),
    .row25(undriven_26), .row26(undriven_27), .row27(undriven_28), .row28(undriven_29), .row29(undriven_30),
    .row30(undriven_31), .row31(undriven_32));
  ROM #(.addrWidth(8), .dataWidth(16), .Select("high")) rom_1 (.addr(CNT), .data(\发送 ));
  \_16位流水接口  \u_16位流水接口_1  (
    .Din16(\发送 ), .\传输状态In_表明当前传输数据有效 (1'b1), .CLK(CLK), .Dout16(\n16位流水接口_1_dout16 ),
    .\传输状态Out_表明当前传输数据有效 (\n16位流水接口_1_传输状态out_表明当前传输数据有效 ), .\同步清零_气泡_高电平有效 (clr2));  // open: 使能端_低电平有效_stall_高电平有效
  \海明编码  \u_海明编码_1  (.\原始数据 (\n16位流水接口_1_dout16 ), .\海明码 (\海明编码_1_海明码 ));
  \_22位流水接口  \u_22位流水接口_1  (
    .Din22(\海明编码_1_海明码 ), .\传输状态In_表明当前传输数据有效 (\n16位流水接口_1_传输状态out_表明当前传输数据有效 ), .CLK(CLK),
    .Dout22(\n22位流水接口_1_dout22 ), .\传输状态Out_表明当前传输数据有效 (\n22位流水接口_1_传输状态out_表明当前传输数据有效 ),
    .\同步清零_气泡_高电平有效 (clr3));  // open: 使能端_低电平有效_stall_高电平有效
  \_22位随机干扰  \u_22位随机干扰_1  (
    .\加扰模式 (2'b11), .\_22位输入 (\n22位流水接口_1_dout22 ), .\加扰后数据 (\n22位随机干扰_1_加扰后数据 ), .\增加三位错 (\加噪 ), .CLK(CLK),
    .EDU(EDU));  // open: 随机加扰屏蔽字
  \国标转区位码  \u_国标转区位码_2  (.\位号 (\国标转区位码_2_位号 ), .\区号 (\国标转区位码_2_区号 ), .GB2312(\接收 ));
  \_22位流水接口  \u_22位流水接口_2  (
    .Din22(\n22位随机干扰_1_加扰后数据 ), .\传输状态In_表明当前传输数据有效 (\n22位流水接口_1_传输状态out_表明当前传输数据有效 ), .CLK(CLK),
    .Dout22(\n22位流水接口_2_dout22 ), .\传输状态Out_表明当前传输数据有效 (\n22位流水接口_2_传输状态out_表明当前传输数据有效 ),
    .\同步清零_气泡_高电平有效 (clr4));  // open: 使能端_低电平有效_stall_高电平有效
  DotMatrix #(.inputtype("row"), .matrixcols(32), .matrixrows(32), .persist(0), .dotshape("circle")) dotmatrix_2 (
    .row0(undriven_33), .row1(undriven_34), .row2(undriven_35), .row3(undriven_36), .row4(undriven_37),
    .row5(undriven_38), .row6(undriven_39), .row7(undriven_40), .row8(undriven_41), .row9(undriven_42),
    .row10(undriven_43), .row11(undriven_44), .row12(undriven_45), .row13(undriven_46), .row14(undriven_47),
    .row15(undriven_48), .row16(undriven_49), .row17(undriven_50), .row18(undriven_51), .row19(undriven_52),
    .row20(undriven_53), .row21(undriven_54), .row22(undriven_55), .row23(undriven_56), .row24(undriven_57),
    .row25(undriven_58), .row26(undriven_59), .row27(undriven_60), .row28(undriven_61), .row29(undriven_62),
    .row30(undriven_63), .row31(undriven_64));
  LED #(.active("true")) \u_两位错  (.in(_2err));
  LED #(.active("true")) \u_一位错  (.in(_1err));
  LED #(.active("true")) \u_无错误  (.in(\海明解码_1__0位错 ));
  \海明解码  \u_海明解码_1  (
    .\_1位错 (_1err), .\_2位错 (_2err), .\_0位错 (\海明解码_1__0位错 ), .\海明码 (\n22位流水接口_2_dout22 ),
    .\纠错后数据 (\海明解码_1_纠错后数据 ));
  \_16位流水接口  \u_16位流水接口_2  (
    .Din16(\海明解码_1_纠错后数据 ), .\传输状态In_表明当前传输数据有效 (\n22位流水接口_2_传输状态out_表明当前传输数据有效 ), .CLK(CLK), .Dout16(\接收 ),
    .\使能端_低电平有效_stall_高电平有效 (en5));  // open: 传输状态Out_表明当前传输数据有效, 同步清零_气泡_高电平有效
  // Probe on \接收 

  // Notes on the sheet:
  //   海明码流水传输电路
  //   寄存器
  //   发送方
  //   汉字显示
  //   加法器
  //   GB2312
  //   1.取数阶段
  //   contents of rom_1 (hex, n*v repeats v):
  //   bbaa d6d0 bfc6 bcbc b4f3 d1a7 cac7 b9fa bcd2 bdcc d3fd b2bf d6b1 caf4 b5c4 c8ab b9fa d6d8 b5e3 b4f3
  //   d1a7 a3ac d3c9 d4ad bbaa d6d0 c0ed b9a4 b4f3 d1a7 a1a2 cdac bcc3 d2bd bfc6 b4f3 d1a7 a1a2 cee4 baba
  //   b3c7 cad0 bda8 c9e8 d1a7 d4ba d3da a3b2 a3b0 a3b0 a3b0 c4ea a3b5 d4c2 a3b2 a3b6 c8d5 bacf b2a2 b3c9
  //   c1a2 a3ac cac7 cad7 c5fa c1d0 c8eb b9fa bcd2 a1b0 a3b2 a3b1 a3b1 b9a4 b3cc a1b1 d6d8 b5e3 bda8 c9e8
  //   bacd b9fa bcd2 a1b0 a3b9 a3b8 a3b5 b9a4 b3cc a1b1 bda8 c9e8 b8df d0a3 d6ae d2bb a1a3 d1a7 d0a3 d0a3
  //   d4b0 d5bc b5d8 c6df c7a7 d3e0 c4b6 a3ac d4b0 c4da caf7 c4be b4d0 dcd7 a3ac b1cc b2dd c8e7 d2f0 a3ac
  //   bbb7 beb3 d3c5 d1c5 a3ac beb0 c9ab d0e3 c0f6 a3ac c2cc bbaf b8b2 b8c7 c2ca 3732 25a3 acb1 bbd3 fece
  //   aaa1 b0c9 adc1 d6ca bdb4 f3d1 a7a1 b1a1
  //   ~使能/Stall
  //   发送方在ROM预存了一段中文文字，通过计数器驱动电路每个时钟传输一个汉字
  //   同步清零
  //   用户实现了国标转区位码电路后，可在中间窗口观察发送方和接收方汉字显示是否一致以观察海明检错纠错性能
  //   数据状态：高电平有效
  //   2.编码阶段
  //   接收方
  //   汉字显示
  //   电路功能：采用流水方式进行数据编码传输，测试海明编码检错纠错能力，当出现2位错时，发送重传信号要求发送方重传，保证接收方按ROM中的地址顺序接受所有汉字
  //   3.传输阶段
  //   4.解码阶段
  //   此电路可帮助学生理解指令流水线工作原理，重传类似指令流水线中的分支指令
  //   5.显示阶段
  //   请将时钟频率调到8Hz
  //   Ctrl+ K启动电路自动仿真
  //   EDUCODER在线测试引脚
  //   请勿增删改引脚
endmodule

module \CRC传输测试1  (
  input  [15:0] \原始数据 ,
  input  [1:0] \加扰控制 
);

  wire clock_1_out, comparator_1_eq, \crc解码_1__0位错 , \crc解码_1__1位错 , \crc解码_1__2位错 ;
  wire [15:0] \crc解码_1_纠错后数据 ;
  wire [21:0] \crc编码_1_crc校验码 , \n22位随机干扰_1_加扰后数据 , \n22位随机干扰_1_随机加扰屏蔽字 ;

  // Probe on \原始数据 
  // Probe on \crc编码_1_crc校验码 
  \CRC编码  \crc编码_1  (.\原始数据 (\原始数据 ), .\CRC校验码 (\crc编码_1_crc校验码 ));
  // Probe on \crc编码_1_crc校验码 
  // Probe on \n22位随机干扰_1_随机加扰屏蔽字 
  Clock #(.highDuration(1), .lowDuration(1)) clock_1 (.out(clock_1_out));
  // Probe on \n22位随机干扰_1_加扰后数据 
  \_22位随机干扰  \u_22位随机干扰_1  (
    .\加扰模式 (\加扰控制 ), .\随机加扰屏蔽字 (\n22位随机干扰_1_随机加扰屏蔽字 ), .\_22位输入 (\crc编码_1_crc校验码 ),
    .\加扰后数据 (\n22位随机干扰_1_加扰后数据 ), .CLK(clock_1_out));  // open: 增加三位错, EDU
  // Probe on \n22位随机干扰_1_加扰后数据 
  LED #(.active("true")) OK (.in(\crc解码_1__0位错 ));
  LED #(.active("true")) \u_两位错  (.in(\crc解码_1__2位错 ));
  LED #(.active("true")) \u_一位错  (.in(\crc解码_1__1位错 ));
  \CRC解码  \crc解码_1  (
    .\CRC编码 (\n22位随机干扰_1_加扰后数据 ), .\_1位错 (\crc解码_1__1位错 ), .\_2位错 (\crc解码_1__2位错 ),
    .\纠错后数据 (\crc解码_1_纠错后数据 ), .\_0位错 (\crc解码_1__0位错 ));
  // Probe on \crc解码_1_纠错后数据 
  Comparator #(.width(16), .mode("twosComplement")) comparator_1 (
    .a(\原始数据 ), .b(\crc解码_1_纠错后数据 ), .eq(comparator_1_eq));  // open: gt, lt
  LED #(.active("true")) \u_数据正确  (.in(comparator_1_eq));

  // Notes on the sheet:
  //   发送方
  //   Ctrl+T 驱动时钟触发随机干扰变化
  //   CRC编解码传输电路
  //   电路功能：测试CRC编解码电路正确性，仿真时设置加扰控制位和原始数据，按CTRL+T触发不同的干扰，检验编解码电路功能
  //   加扰控制00：不加扰  01:1位加扰 10:2位加扰 11：随机加扰
  //   接收方
endmodule

module \CRC传输测试2  (
  input  [1:0] \加扰控制 
);

  wire CLK, comparator_1_eq, \crc解码_1__0位错 , \crc解码_1__1位错 , \crc解码_1__2位错 ;
  wire [6:0] \国标转区位码_1_位号 , \国标转区位码_1_区号 , \国标转区位码_2_位号 , \国标转区位码_2_区号 ;
  wire [7:0] counter_1_q;
  wire [15:0] \发送 , \接收 ;
  wire [21:0] \crc编码_1_crc校验码 , \n22位随机干扰_1_加扰后数据 , \n22位随机干扰_1_随机加扰屏蔽字 ;
  wire [31:0] undriven, undriven_2, undriven_3, undriven_4, undriven_5, undriven_6, undriven_7, undriven_8,
       undriven_9, undriven_10, undriven_11, undriven_12, undriven_13, undriven_14, undriven_15, undriven_16,
       undriven_17, undriven_18, undriven_19, undriven_20, undriven_21, undriven_22, undriven_23,
       undriven_24, undriven_25, undriven_26, undriven_27, undriven_28, undriven_29, undriven_30,
       undriven_31, undriven_32, undriven_33, undriven_34, undriven_35, undriven_36, undriven_37,
       undriven_38, undriven_39, undriven_40, undriven_41, undriven_42, undriven_43, undriven_44,
       undriven_45, undriven_46, undriven_47, undriven_48, undriven_49, undriven_50, undriven_51,
       undriven_52, undriven_53, undriven_54, undriven_55, undriven_56, undriven_57, undriven_58,
       undriven_59, undriven_60, undriven_61, undriven_62, undriven_63, undriven_64;

  Counter #(.width(8), .max('hff), .ongoal("wrap"), .trigger("rising"), .behavior("old")) counter_1 (
    .Q(counter_1_q), .clk(CLK));  // open: load, D, count, carry, clr, preset
  Clock #(.highDuration(1), .lowDuration(1)) \u_时钟  (.out(CLK));
  \国标转区位码  \u_国标转区位码_1  (.\位号 (\国标转区位码_1_位号 ), .\区号 (\国标转区位码_1_区号 ), .GB2312(\发送 ));
  DotMatrix #(.inputtype("row"), .matrixcols(32), .matrixrows(32), .persist(0), .dotshape("circle")) dotmatrix_1 (
    .row0(undriven), .row1(undriven_2), .row2(undriven_3), .row3(undriven_4), .row4(undriven_5),
    .row5(undriven_6), .row6(undriven_7), .row7(undriven_8), .row8(undriven_9), .row9(undriven_10),
    .row10(undriven_11), .row11(undriven_12), .row12(undriven_13), .row13(undriven_14), .row14(undriven_15),
    .row15(undriven_16), .row16(undriven_17), .row17(undriven_18), .row18(undriven_19), .row19(undriven_20),
    .row20(undriven_21), .row21(undriven_22), .row22(undriven_23), .row23(undriven_24), .row24(undriven_25),
    .row25(undriven_26), .row26(undriven_27), .row27(undriven_28), .row28(undriven_29), .row29(undriven_30),
    .row30(undriven_31), .row31(undriven_32));
  ROM #(.addrWidth(8), .dataWidth(16), .Select("high")) rom_1 (.addr(counter_1_q), .data(\发送 ));
  // Probe on \发送 
  // Probe on \crc编码_1_crc校验码 
  \CRC编码  \crc编码_1  (.\原始数据 (\发送 ), .\CRC校验码 (\crc编码_1_crc校验码 ));
  // Probe on \crc编码_1_crc校验码 
  // Probe on \n22位随机干扰_1_随机加扰屏蔽字 
  \_22位随机干扰  \u_22位随机干扰_1  (
    .\加扰模式 (\加扰控制 ), .\随机加扰屏蔽字 (\n22位随机干扰_1_随机加扰屏蔽字 ), .\_22位输入 (\crc编码_1_crc校验码 ),
    .\加扰后数据 (\n22位随机干扰_1_加扰后数据 ), .CLK(CLK));  // open: 增加三位错, EDU
  \国标转区位码  \u_国标转区位码_2  (.\位号 (\国标转区位码_2_位号 ), .\区号 (\国标转区位码_2_区号 ), .GB2312(\接收 ));
  // Probe on \n22位随机干扰_1_加扰后数据 
  // Probe on \n22位随机干扰_1_加扰后数据 
  LED #(.active("true")) \u_一位错  (.in(\crc解码_1__1位错 ));
  LED #(.active("true")) \u_两位错  (.in(\crc解码_1__2位错 ));
  LED #(.active("true")) \u_无错误  (.in(\crc解码_1__0位错 ));
  DotMatrix #(.inputtype("row"), .matrixcols(32), .matrixrows(32), .persist(0), .dotshape("circle")) dotmatrix_2 (
    .row0(undriven_33), .row1(undriven_34), .row2(undriven_35), .row3(undriven_36), .row4(undriven_37),
    .row5(undriven_38), .row6(undriven_39), .row7(undriven_40), .row8(undriven_41), .row9(undriven_42),
    .row10(undriven_43), .row11(undriven_44), .row12(undriven_45), .row13(undriven_46), .row14(undriven_47),
    .row15(undriven_48), .row16(undriven_49), .row17(undriven_50), .row18(undriven_51), .row19(undriven_52),
    .row20(undriven_53), .row21(undriven_54), .row22(undriven_55), .row23(undriven_56), .row24(undriven_57),
    .row25(undriven_58), .row26(undriven_59), .row27(undriven_60), .row28(undriven_61), .row29(undriven_62),
    .row30(undriven_63), .row31(undriven_64));
  \CRC解码  \crc解码_1  (
    .\CRC编码 (\n22位随机干扰_1_加扰后数据 ), .\_1位错 (\crc解码_1__1位错 ), .\_2位错 (\crc解码_1__2位错 ), .\纠错后数据 (\接收 ),
    .\_0位错 (\crc解码_1__0位错 ));
  // Probe on \接收 
  Comparator #(.width(16), .mode("twosComplement")) comparator_1 (
    .a(\发送 ), .b(\接收 ), .eq(comparator_1_eq));  // open: gt, lt
  LED #(.active("true")) \u_数据正确  (.in(comparator_1_eq));

  // Notes on the sheet:
  //   发送方
  //   计数器
  //   发送方
  //   汉字显示
  //   GB2312
  //   contents of rom_1 (hex, n*v repeats v):
  //   bbaa d6d0 bfc6 bcbc b4f3 d1a7 cac7 b9fa bcd2 bdcc d3fd b2bf d6b1 caf4 b5c4 c8ab b9fa d6d8 b5e3 b4f3
  //   d1a7 a3ac d3c9 d4ad bbaa d6d0 c0ed b9a4 b4f3 d1a7 a1a2 cdac bcc3 d2bd bfc6 b4f3 d1a7 a1a2 cee4 baba
  //   b3c7 cad0 bda8 c9e8 d1a7 d4ba d3da a3b2 a3b0 a3b0 a3b0 c4ea a3b5 d4c2 a3b2 a3b6 c8d5 bacf b2a2 b3c9
  //   c1a2 a3ac cac7 cad7 c5fa c1d0 c8eb b9fa bcd2 a1b0 a3b2 a3b1 a3b1 b9a4 b3cc a1b1 d6d8 b5e3 bda8 c9e8
  //   bacd b9fa bcd2 a1b0 a3b9 a3b8 a3b5 b9a4 b3cc a1b1 bda8 c9e8 b8df d0a3 d6ae d2bb a1a3 d1a7 d0a3 d0a3
  //   d4b0 d5bc b5d8 c6df c7a7 d3e0 c4b6 a3ac d4b0 c4da caf7 c4be b4d0 dcd7 a3ac b1cc b2dd c8e7 d2f0 a3ac
  //   bbb7 beb3 d3c5 d1c5 a3ac beb0 c9ab d0e3 c0f6 a3ac c2cc bbaf b8b2 b8c7 c2ca 3732 25a3 acb1 bbd3 fece
  //   aaa1 b0c9 adc1 d6ca bdb4 f3d1 a7a1 b1a1
  //   Ctrl+T 驱动时钟触发随机干扰变化
  //   电路功能：测试CRC编解码电路正确性，仿真时设置加扰控制位和原始数据，按CTRL+T触发不同的干扰，检验编解码电路功能
  //   发送方在ROM预存了一段中文文字，通过计数器驱动电路每个时钟传输一个汉字到接收方
  //   用户实现了国标转区位码电路后，可在中间窗口观察发送方和接收方汉字显示是否一致以观察海明检错纠错性能
  //   CRC编解码传输电路
  //   接收方
  //   汉字显示
  //   Ctrl+T 驱动时钟触发随机干扰变化
  //   加扰控制00：不加扰  01:1位加扰 10:2位加扰 11：随机加扰
  //   加扰控制00：不加扰  01:1位加扰 10:2位加扰 11：随机加扰
  //   接收方
  //   请将时钟频率调到8Hz
endmodule

// CRC
module \CRC编码流水传输  (
  input  \加噪 ,
  input  EDU,
  output _1err,
  output _2err,
  output clr2,
  output clr3,
  output clr4,
  output en5
);

  wire CLK, \crc解码_1__0位错 , \n16位流水接口_1_传输状态out_表明当前传输数据有效 , \n22位流水接口_1_传输状态out_表明当前传输数据有效 ,
       \n22位流水接口_2_传输状态out_表明当前传输数据有效 ;
  wire [6:0] \国标转区位码_1_位号 , \国标转区位码_1_区号 , \国标转区位码_2_位号 , \国标转区位码_2_区号 ;
  wire [7:0] adder_1_out, CNT;
  wire [15:0] \crc解码_1_纠错后数据 , \n16位流水接口_1_dout16 , \发送 , \接收 ;
  wire [21:0] \crc编码_1_crc校验码 , \n22位流水接口_1_dout22 , \n22位流水接口_2_dout22 , \n22位随机干扰_1_加扰后数据 ;
  wire [31:0] undriven, undriven_2, undriven_3, undriven_4, undriven_5, undriven_6, undriven_7, undriven_8,
       undriven_9, undriven_10, undriven_11, undriven_12, undriven_13, undriven_14, undriven_15, undriven_16,
       undriven_17, undriven_18, undriven_19, undriven_20, undriven_21, undriven_22, undriven_23,
       undriven_24, undriven_25, undriven_26, undriven_27, undriven_28, undriven_29, undriven_30,
       undriven_31, undriven_32, undriven_33, undriven_34, undriven_35, undriven_36, undriven_37,
       undriven_38, undriven_39, undriven_40, undriven_41, undriven_42, undriven_43, undriven_44,
       undriven_45, undriven_46, undriven_47, undriven_48, undriven_49, undriven_50, undriven_51,
       undriven_52, undriven_53, undriven_54, undriven_55, undriven_56, undriven_57, undriven_58,
       undriven_59, undriven_60, undriven_61, undriven_62, undriven_63, undriven_64;

  Register #(.width(8), .trigger("rising"), .Select("low")) register_1 (
    .D(adder_1_out), .Q(CNT), .clk(CLK));  // open: en, clr
  Clock #(.highDuration(1), .lowDuration(1)) \u_时钟  (.out(CLK));
  \国标转区位码  \u_国标转区位码_1  (.\位号 (\国标转区位码_1_位号 ), .\区号 (\国标转区位码_1_区号 ), .GB2312(\发送 ));
  Adder #(.width(8)) adder_1 (.a(8'h1), .b(CNT), .out(adder_1_out));  // open: cin, cout
  DotMatrix #(.inputtype("row"), .matrixcols(32), .matrixrows(32), .persist(0), .dotshape("circle")) dotmatrix_1 (
    .row0(undriven), .row1(undriven_2), .row2(undriven_3), .row3(undriven_4), .row4(undriven_5),
    .row5(undriven_6), .row6(undriven_7), .row7(undriven_8), .row8(undriven_9), .row9(undriven_10),
    .row10(undriven_11), .row11(undriven_12), .row12(undriven_13), .row13(undriven_14), .row14(undriven_15),
    .row15(undriven_16), .row16(undriven_17), .row17(undriven_18), .row18(undriven_19), .row19(undriven_20),
    .row20(undriven_21), .row21(undriven_22), .row22(undriven_23), .row23(undriven_24), .row24(undriven_25),
    .row25(undriven_26), .row26(undriven_27), .row27(undriven_28), .row28(undriven_29), .row29(undriven_30),
    .row30(undriven_31), .row31(undriven_32));
  ROM #(.addrWidth(8), .dataWidth(16), .Select("high")) rom_1 (.addr(CNT), .data(\发送 ));
  \_16位流水接口  \u_16位流水接口_1  (
    .Din16(\发送 ), .\传输状态In_表明当前传输数据有效 (1'b1), .CLK(CLK), .Dout16(\n16位流水接口_1_dout16 ),
    .\传输状态Out_表明当前传输数据有效 (\n16位流水接口_1_传输状态out_表明当前传输数据有效 ), .\同步清零_气泡_高电平有效 (clr2));  // open: 使能端_低电平有效_stall_高电平有效
  \CRC编码  \crc编码_1  (.\原始数据 (\n16位流水接口_1_dout16 ), .\CRC校验码 (\crc编码_1_crc校验码 ));
  \_22位流水接口  \u_22位流水接口_1  (
    .Din22(\crc编码_1_crc校验码 ), .\传输状态In_表明当前传输数据有效 (\n16位流水接口_1_传输状态out_表明当前传输数据有效 ), .CLK(CLK),
    .Dout22(\n22位流水接口_1_dout22 ), .\传输状态Out_表明当前传输数据有效 (\n22位流水接口_1_传输状态out_表明当前传输数据有效 ),
    .\同步清零_气泡_高电平有效 (clr3));  // open: 使能端_低电平有效_stall_高电平有效
  \_22位随机干扰  \u_22位随机干扰_1  (
    .\加扰模式 (2'b11), .\_22位输入 (\n22位流水接口_1_dout22 ), .\加扰后数据 (\n22位随机干扰_1_加扰后数据 ), .\增加三位错 (\加噪 ), .CLK(CLK),
    .EDU(EDU));  // open: 随机加扰屏蔽字
  \国标转区位码  \u_国标转区位码_2  (.\位号 (\国标转区位码_2_位号 ), .\区号 (\国标转区位码_2_区号 ), .GB2312(\接收 ));
  \_22位流水接口  \u_22位流水接口_2  (
    .Din22(\n22位随机干扰_1_加扰后数据 ), .\传输状态In_表明当前传输数据有效 (\n22位流水接口_1_传输状态out_表明当前传输数据有效 ), .CLK(CLK),
    .Dout22(\n22位流水接口_2_dout22 ), .\传输状态Out_表明当前传输数据有效 (\n22位流水接口_2_传输状态out_表明当前传输数据有效 ),
    .\同步清零_气泡_高电平有效 (clr4));  // open: 使能端_低电平有效_stall_高电平有效
  DotMatrix #(.inputtype("row"), .matrixcols(32), .matrixrows(32), .persist(0), .dotshape("circle")) dotmatrix_2 (
    .row0(undriven_33), .row1(undriven_34), .row2(undriven_35), .row3(undriven_36), .row4(undriven_37),
    .row5(undriven_38), .row6(undriven_39), .row7(undriven_40), .row8(undriven_41), .row9(undriven_42),
    .row10(undriven_43), .row11(undriven_44), .row12(undriven_45), .row13(undriven_46), .row14(undriven_47),
    .row15(undriven_48), .row16(undriven_49), .row17(undriven_50), .row18(undriven_51), .row19(undriven_52),
    .row20(undriven_53), .row21(undriven_54), .row22(undriven_55), .row23(undriven_56), .row24(undriven_57),
    .row25(undriven_58), .row26(undriven_59), .row27(undriven_60), .row28(undriven_61), .row29(undriven_62),
    .row30(undriven_63), .row31(undriven_64));
  LED #(.active("true")) \u_一位错  (.in(_1err));
  LED #(.active("true")) \u_两位错  (.in(_2err));
  LED #(.active("true")) \u_无错误  (.in(\crc解码_1__0位错 ));
  \CRC解码  \crc解码_1  (
    .\CRC编码 (\n22位流水接口_2_dout22 ), .\_1位错 (_1err), .\_2位错 (_2err), .\纠错后数据 (\crc解码_1_纠错后数据 ),
    .\_0位错 (\crc解码_1__0位错 ));
  \_16位流水接口  \u_16位流水接口_2  (
    .Din16(\crc解码_1_纠错后数据 ), .\传输状态In_表明当前传输数据有效 (\n22位流水接口_2_传输状态out_表明当前传输数据有效 ), .CLK(CLK), .Dout16(\接收 ),
    .\使能端_低电平有效_stall_高电平有效 (en5));  // open: 传输状态Out_表明当前传输数据有效, 同步清零_气泡_高电平有效
  // Probe on \接收 

  // Notes on the sheet:
  //   CRC编码流水传输电路
  //   寄存器
  //   发送方
  //   汉字显示
  //   加法器
  //   GB2312
  //   1.取数阶段
  //   contents of rom_1 (hex, n*v repeats v):
  //   bbaa d6d0 bfc6 bcbc b4f3 d1a7 cac7 b9fa bcd2 bdcc d3fd b2bf d6b1 caf4 b5c4 c8ab b9fa d6d8 b5e3 b4f3
  //   d1a7 a3ac d3c9 d4ad bbaa d6d0 c0ed b9a4 b4f3 d1a7 a1a2 cdac bcc3 d2bd bfc6 b4f3 d1a7 a1a2 cee4 baba
  //   b3c7 cad0 bda8 c9e8 d1a7 d4ba d3da a3b2 a3b0 a3b0 a3b0 c4ea a3b5 d4c2 a3b2 a3b6 c8d5 bacf b2a2 b3c9
  //   c1a2 a3ac cac7 cad7 c5fa c1d0 c8eb b9fa bcd2 a1b0 a3b2 a3b1 a3b1 b9a4 b3cc a1b1 d6d8 b5e3 bda8 c9e8
  //   bacd b9fa bcd2 a1b0 a3b9 a3b8 a3b5 b9a4 b3cc a1b1 bda8 c9e8 b8df d0a3 d6ae d2bb a1a3 d1a7 d0a3 d0a3
  //   d4b0 d5bc b5d8 c6df c7a7 d3e0 c4b6 a3ac d4b0 c4da caf7 c4be b4d0 dcd7 a3ac b1cc b2dd c8e7 d2f0 a3ac
  //   bbb7 beb3 d3c5 d1c5 a3ac beb0 c9ab d0e3 c0f6 a3ac c2cc bbaf b8b2 b8c7 c2ca 3732 25a3 acb1 bbd3 fece
  //   aaa1 b0c9 adc1 d6ca bdb4 f3d1 a7a1 b1a1
  //   ~使能/Stall
  //   发送方在ROM预存了一段中文文字，通过计数器驱动电路每个时钟传输一个汉字
  //   同步清零
  //   用户实现了国标转区位码电路后，可在中间窗口观察发送方和接收方汉字显示是否一致以观察海明检错纠错性能
  //   数据状态：高电平有效
  //   2.编码阶段
  //   接收方
  //   汉字显示
  //   电路功能：采用流水方式进行数据编码传输，测试海明编码检错纠错能力，当出现2位错时，发送重传信号要求发送方重传，保证接收方按ROM中的地址顺序接受所有汉字
  //   3.传输阶段
  //   4.解码阶段
  //   此电路可帮助学生理解指令流水线工作原理，重传类似指令流水线中的分支指令
  //   5.显示阶段
  //   请将时钟频率调到8Hz
  //   Ctrl+ K启动电路自动仿真
  //   EDUCODER在线测试引脚
  //   请勿增删改引脚
endmodule

// 随机干扰
module \_22位随机干扰  (
  input  CLK,
  input  [21:0] \_22位输入 ,
  input  EDU,
  input  [1:0] \加扰模式 ,
  input  \增加三位错 ,
  output [21:0] \随机加扰屏蔽字 ,
  output [21:0] \加扰后数据 
);

  wire comparator_1_eq, \随机信号_5_out ;
  wire [1:0] EDUerr, multiplexer_3_out, \随机信号_4_out ;
  wire [3:0] \随机信号_2_out , \随机信号_3_out , \随机信号_out ;
  wire [7:0] counter_1_q;
  wire [15:0] \_1位加扰A ;
  wire [21:0] \_1位加扰 , \_2位加扰 , \_3位加扰 , multiplexer_1_out, multiplexer_5_out, shifter_1_out, \随机加扰 ;
  wire [21:6] \_1位加扰B , \_1位加扰C ;

  Random #(.width(4), .seed(0), .trigger("rising")) \u_随机信号  (.clk(CLK), .out(\随机信号_out ));  // open: next, clr
  Decoder #(.select(4), .tristate("false"), .disabled("Z"), .enable("false")) decoder_1 (
    .out0(\_1位加扰A [0]), .out1(\_1位加扰A [1]), .out2(\_1位加扰A [2]), .out3(\_1位加扰A [3]), .out4(\_1位加扰A [4]),
    .out5(\_1位加扰A [5]), .out6(\_1位加扰A [6]), .out7(\_1位加扰A [7]), .out8(\_1位加扰A [8]), .out9(\_1位加扰A [9]),
    .out10(\_1位加扰A [10]), .out11(\_1位加扰A [11]), .out12(\_1位加扰A [12]), .out13(\_1位加扰A [13]),
    .out14(\_1位加扰A [14]), .out15(\_1位加扰A [15]), .sel(\随机信号_out ));
  Decoder #(.select(4), .tristate("false"), .disabled("Z"), .enable("false")) decoder_2 (
    .out0(\_1位加扰B [6]), .out1(\_1位加扰B [7]), .out2(\_1位加扰B [8]), .out3(\_1位加扰B [9]), .out4(\_1位加扰B [10]),
    .out5(\_1位加扰B [11]), .out6(\_1位加扰B [12]), .out7(\_1位加扰B [13]), .out8(\_1位加扰B [14]), .out9(\_1位加扰B [15]),
    .out10(\_1位加扰B [16]), .out11(\_1位加扰B [17]), .out12(\_1位加扰B [18]), .out13(\_1位加扰B [19]),
    .out14(\_1位加扰B [20]), .out15(\_1位加扰B [21]), .sel(\随机信号_2_out ));
  Random #(.width(4), .seed(18), .trigger("rising")) \u_随机信号_2  (.clk(CLK), .out(\随机信号_2_out ));  // open: next, clr
  Random #(.width(4), .seed(3), .trigger("rising")) \u_随机信号_3  (.clk(CLK), .out(\随机信号_3_out ));  // open: next, clr
  Random #(.width(2), .seed(21), .trigger("rising")) \u_随机信号_4  (.clk(CLK), .out(\随机信号_4_out ));  // open: next, clr
  Random #(.width(1), .seed(31), .trigger("rising")) \u_随机信号_5  (.clk(CLK), .out(\随机信号_5_out ));  // open: next, clr
  Decoder #(.select(4), .tristate("false"), .disabled("Z"), .enable("false")) decoder_3 (
    .out0(\_1位加扰C [6]), .out1(\_1位加扰C [7]), .out2(\_1位加扰C [8]), .out3(\_1位加扰C [9]), .out4(\_1位加扰C [10]),
    .out5(\_1位加扰C [11]), .out6(\_1位加扰C [12]), .out7(\_1位加扰C [13]), .out8(\_1位加扰C [14]), .out9(\_1位加扰C [15]),
    .out10(\_1位加扰C [16]), .out11(\_1位加扰C [17]), .out12(\_1位加扰C [18]), .out13(\_1位加扰C [19]),
    .out14(\_1位加扰C [20]), .out15(\_1位加扰C [21]), .sel(\随机信号_3_out ));
  Pull_Resistor #(.pull(1)) pull_resistor_1 (.node(\加扰模式 ));
  Pull_Resistor #(.pull(0)) pull_resistor_2 (.node(\增加三位错 ));
  Multiplexer #(.select(1), .width(22), .disabled("Z"), .enable("false")) multiplexer_1 (
    .in0({\_1位加扰B , {6{1'b0}}}), .in1(\_3位加扰 ), .out(multiplexer_1_out), .sel(\增加三位错 ));
  Multiplexer #(.select(2), .width(22), .disabled("Z"), .enable("false")) multiplexer_2 (
    .in0({22{1'b0}}), .in1({{6{1'b0}}, \_1位加扰A }), .in2(\_2位加扰 ), .in3(multiplexer_1_out), .out(\随机加扰 ),
    .sel(\随机信号_4_out ));
  Pull_Resistor #(.pull(0)) pull_resistor_3 (.node(EDU));
  Multiplexer #(.select(1), .width(2), .disabled("Z"), .enable("false")) multiplexer_3 (
    .in0(\加扰模式 ), .in1(EDUerr), .out(multiplexer_3_out), .sel(EDU));
  Shifter #(.width(22), .shift("rl")) shifter_1 (.in({{6{1'b0}}, \_1位加扰A }), .\dist (5'b00001), .out(shifter_1_out));
  Comparator #(.width(22), .mode("unsigned")) comparator_1 (
    .a({{6{1'b0}}, \_1位加扰A }), .b({\_1位加扰B , {6{1'b0}}}), .eq(comparator_1_eq));  // open: gt, lt
  Multiplexer #(.select(2), .width(22), .disabled("Z"), .enable("false")) multiplexer_4 (
    .in0({22{1'b0}}), .in1(\_1位加扰 ), .in2(\_2位加扰 ), .in3(\随机加扰 ), .out(\随机加扰屏蔽字 ), .sel(multiplexer_3_out));
  Multiplexer #(.select(1), .width(22), .disabled("Z"), .enable("false")) multiplexer_5 (
    .in0({{6{1'b0}}, \_1位加扰A }), .in1(shifter_1_out), .out(multiplexer_5_out), .sel(comparator_1_eq));
  Counter #(.width(8), .max('hff), .ongoal("wrap"), .trigger("rising"), .behavior("old")) counter_1 (
    .Q(counter_1_q), .clk(CLK));  // open: load, D, count, carry, clr, preset
  assign \_2位加扰  = multiplexer_5_out ^ {\_1位加扰B , {6{1'b0}}};  // XOR_Gate xor_1, 22 bits wide
  assign \_3位加扰  = \_2位加扰  ^ {\_1位加扰C , {6{1'b0}}};  // XOR_Gate xor_2, 22 bits wide
  ROM #(.addrWidth(8), .dataWidth(2), .Select("low")) rom_1 (.addr(counter_1_q), .data(EDUerr));
  Multiplexer #(.select(1), .width(22), .disabled("Z"), .enable("false")) multiplexer_6 (
    .in0(multiplexer_5_out), .in1({\_1位加扰B , {6{1'b0}}}), .out(\_1位加扰 ), .sel(\随机信号_5_out ));
  assign \加扰后数据  = \随机加扰屏蔽字  ^ \_22位输入 ;  // XOR_Gate xor_3, 22 bits wide

  // Notes on the sheet:
  //   在随机加扰模式中增加三位错
  //   两个随机信号分别负责高16位和第16位
  //   22位信道加扰屏蔽字生成电路，加扰模式引脚00：不加扰  01:1位加扰 10:2位加扰 11：0-2位随机加扰
  //   如果两个信号相同，其中一个移位
  //   contents of rom_1 (hex, n*v repeats v):
  //   2 2 1 1 1 4*0 4*2 1 1 1 0 1 0 0 2 0 2 5*0 1 0 1 4*0 2
endmodule

// 随机加扰
module \_17位随机干扰  (
  input  CLK,
  input  [16:0] \_17位输入 ,
  output [16:0] \随机加扰屏蔽字 ,
  output [16:0] \加扰后数据 
);

  wire [4:0] \随机数_2_out , \随机数_3_out , \随机数_out ;
  wire [16:0] or_1_out;
  wire [31:0] decoder_1_out31, decoder_2_out31, decoder_3_out31;

  Random #(.width(5), .seed(0), .trigger("rising")) \u_随机数  (.clk(CLK), .out(\随机数_out ));  // open: next, clr
  Decoder #(.select(5), .tristate("false"), .disabled("Z"), .enable("false")) decoder_1 (
    .out0(decoder_1_out31[31]), .out1(decoder_1_out31[30]), .out2(decoder_1_out31[29]),
    .out3(decoder_1_out31[28]), .out4(decoder_1_out31[27]), .out5(decoder_1_out31[26]),
    .out6(decoder_1_out31[25]), .out7(decoder_1_out31[24]), .out8(decoder_1_out31[23]),
    .out9(decoder_1_out31[22]), .out10(decoder_1_out31[21]), .out11(decoder_1_out31[20]),
    .out12(decoder_1_out31[19]), .out13(decoder_1_out31[18]), .out14(decoder_1_out31[17]),
    .out15(decoder_1_out31[16]), .out16(decoder_1_out31[15]), .out17(decoder_1_out31[14]),
    .out18(decoder_1_out31[13]), .out19(decoder_1_out31[12]), .out20(decoder_1_out31[11]),
    .out21(decoder_1_out31[10]), .out22(decoder_1_out31[9]), .out23(decoder_1_out31[8]),
    .out24(decoder_1_out31[7]), .out25(decoder_1_out31[6]), .out26(decoder_1_out31[5]),
    .out27(decoder_1_out31[4]), .out28(decoder_1_out31[3]), .out29(decoder_1_out31[2]),
    .out30(decoder_1_out31[1]), .out31(decoder_1_out31[0]), .sel(\随机数_out ));
  Decoder #(.select(5), .tristate("false"), .disabled("Z"), .enable("false")) decoder_2 (
    .out0(decoder_2_out31[31]), .out1(decoder_2_out31[30]), .out2(decoder_2_out31[29]),
    .out3(decoder_2_out31[28]), .out4(decoder_2_out31[27]), .out5(decoder_2_out31[26]),
    .out6(decoder_2_out31[25]), .out7(decoder_2_out31[24]), .out8(decoder_2_out31[23]),
    .out9(decoder_2_out31[22]), .out10(decoder_2_out31[21]), .out11(decoder_2_out31[20]),
    .out12(decoder_2_out31[19]), .out13(decoder_2_out31[18]), .out14(decoder_2_out31[17]),
    .out15(decoder_2_out31[16]), .out16(decoder_2_out31[15]), .out17(decoder_2_out31[14]),
    .out18(decoder_2_out31[13]), .out19(decoder_2_out31[12]), .out20(decoder_2_out31[11]),
    .out21(decoder_2_out31[10]), .out22(decoder_2_out31[9]), .out23(decoder_2_out31[8]),
    .out24(decoder_2_out31[7]), .out25(decoder_2_out31[6]), .out26(decoder_2_out31[5]),
    .out27(decoder_2_out31[4]), .out28(decoder_2_out31[3]), .out29(decoder_2_out31[2]),
    .out30(decoder_2_out31[1]), .out31(decoder_2_out31[0]), .sel(\随机数_2_out ));
  Random #(.width(5), .seed(18), .trigger("rising")) \u_随机数_2  (.clk(CLK), .out(\随机数_2_out ));  // open: next, clr
  Decoder #(.select(5), .tristate("false"), .disabled("Z"), .enable("false")) decoder_3 (
    .out0(decoder_3_out31[31]), .out1(decoder_3_out31[30]), .out2(decoder_3_out31[29]),
    .out3(decoder_3_out31[28]), .out4(decoder_3_out31[27]), .out5(decoder_3_out31[26]),
    .out6(decoder_3_out31[25]), .out7(decoder_3_out31[24]), .out8(decoder_3_out31[23]),
    .out9(decoder_3_out31[22]), .out10(decoder_3_out31[21]), .out11(decoder_3_out31[20]),
    .out12(decoder_3_out31[19]), .out13(decoder_3_out31[18]), .out14(decoder_3_out31[17]),
    .out15(decoder_3_out31[16]), .out16(decoder_3_out31[15]), .out17(decoder_3_out31[14]),
    .out18(decoder_3_out31[13]), .out19(decoder_3_out31[12]), .out20(decoder_3_out31[11]),
    .out21(decoder_3_out31[10]), .out22(decoder_3_out31[9]), .out23(decoder_3_out31[8]),
    .out24(decoder_3_out31[7]), .out25(decoder_3_out31[6]), .out26(decoder_3_out31[5]),
    .out27(decoder_3_out31[4]), .out28(decoder_3_out31[3]), .out29(decoder_3_out31[2]),
    .out30(decoder_3_out31[1]), .out31(decoder_3_out31[0]), .sel(\随机数_3_out ));
  Random #(.width(5), .seed(3), .trigger("rising")) \u_随机数_3  (.clk(CLK), .out(\随机数_3_out ));  // open: next, clr
  assign or_1_out = decoder_1_out31[16:0] | decoder_2_out31[16:0];  // OR_Gate or_1, 17 bits wide
  assign \随机加扰屏蔽字  = or_1_out | decoder_3_out31[16:0];  // OR_Gate or_2, 17 bits wide
  assign \加扰后数据  = \随机加扰屏蔽字  ^ \_17位输入 ;  // XOR_Gate xor_1, 17 bits wide
endmodule

module \_22位流水接口  (
  input  [21:0] Din22,
  input  \传输状态In_表明当前传输数据有效 ,
  input  CLK,
  input  \同步清零_气泡_高电平有效 ,
  input  \使能端_低电平有效_stall_高电平有效 ,
  output [21:0] Dout22,
  output \传输状态Out_表明当前传输数据有效 
);

  wire multiplexer_2_out, pull_resistor_2_node;
  wire [21:0] multiplexer_1_out;

  Multiplexer #(.select(1), .width(22), .disabled("Z"), .enable("false")) multiplexer_1 (
    .in0(Din22), .in1({22{1'b0}}), .out(multiplexer_1_out), .sel(\同步清零_气泡_高电平有效 ));
  Multiplexer #(.select(1), .width(1), .disabled("Z"), .enable("false")) multiplexer_2 (
    .in0(\传输状态In_表明当前传输数据有效 ), .in1(1'b0), .out(multiplexer_2_out), .sel(\同步清零_气泡_高电平有效 ));
  Pull_Resistor #(.pull(0)) pull_resistor_1 (.node(\同步清零_气泡_高电平有效 ));
  Register #(.width(22), .trigger("rising"), .Select("low")) register_1 (
    .D(multiplexer_1_out), .en(pull_resistor_2_node), .Q(Dout22), .clk(CLK));  // open: clr
  Register #(.width(1), .trigger("rising"), .Select("low")) register_2 (
    .D(multiplexer_2_out), .en(pull_resistor_2_node), .Q(\传输状态Out_表明当前传输数据有效 ), .clk(CLK));  // open: clr
  Pull_Resistor #(.pull(0)) pull_resistor_2 (.node(pull_resistor_2_node));
  not not_1 (pull_resistor_2_node, \使能端_低电平有效_stall_高电平有效 );

  // Notes on the sheet:
  //   使能端_低电平有效_stall_高电平有效: pull=down
  //   同步清零_气泡_高电平有效: pull=down
endmodule

module \_16位流水接口  (
  input  [15:0] Din16,
  input  \传输状态In_表明当前传输数据有效 ,
  input  CLK,
  input  \同步清零_气泡_高电平有效 ,
  input  \使能端_低电平有效_stall_高电平有效 ,
  output [15:0] Dout16,
  output \传输状态Out_表明当前传输数据有效 
);

  wire multiplexer_2_out, pull_resistor_2_node;
  wire [15:0] multiplexer_1_out;

  Multiplexer #(.select(1), .width(16), .disabled("Z"), .enable("false")) multiplexer_1 (
    .in0(Din16), .in1({16{1'b0}}), .out(multiplexer_1_out), .sel(\同步清零_气泡_高电平有效 ));
  Multiplexer #(.select(1), .width(1), .disabled("Z"), .enable("false")) multiplexer_2 (
    .in0(\传输状态In_表明当前传输数据有效 ), .in1(1'b0), .out(multiplexer_2_out), .sel(\同步清零_气泡_高电平有效 ));
  Pull_Resistor #(.pull(0)) pull_resistor_1 (.node(\同步清零_气泡_高电平有效 ));
  Register #(.width(16), .trigger("rising"), .Select("low")) register_1 (
    .D(multiplexer_1_out), .en(pull_resistor_2_node), .Q(Dout16), .clk(CLK));  // open: clr
  Register #(.width(1), .trigger("rising"), .Select("low")) register_2 (
    .D(multiplexer_2_out), .en(pull_resistor_2_node), .Q(\传输状态Out_表明当前传输数据有效 ), .clk(CLK));  // open: clr
  Pull_Resistor #(.pull(0)) pull_resistor_2 (.node(pull_resistor_2_node));
  not not_1 (pull_resistor_2_node, \使能端_低电平有效_stall_高电平有效 );
endmodule

module \流水模拟  (
);

  wire \时钟_out ;
  wire [15:0] counter_1_q, \n16位流水接口_1_dout16 , \n16位流水接口_2_dout16 , \n16位流水接口_3_dout16 ,
       \n16位流水接口_4_dout16 , \组合逻辑_1_out_2 , \组合逻辑_2_out_2 , \组合逻辑_3_out_2 ;

  Clock #(.highDuration(1), .lowDuration(1)) \u_时钟  (.out(\时钟_out ));
  Counter #(.width(16), .max('hffff), .ongoal("wrap"), .trigger("rising"), .behavior("old")) counter_1 (
    .Q(counter_1_q), .clk(\时钟_out ));  // open: load, D, count, carry, clr, preset
  // Probe on counter_1_q
  \_16位流水接口  \u_16位流水接口_1  (
    .Din16(counter_1_q), .CLK(\时钟_out ), .Dout16(\n16位流水接口_1_dout16 ));  // open: 传输状态In_表明当前传输数据有效, 传输状态Out_表明当前传输数据有效, 同步清零_气泡_高电平有效, 使能端_低电平有效_stall_高电平有效
  // Probe on \n16位流水接口_1_dout16 
  \组合逻辑  \u_组合逻辑_1  (.in_1(\n16位流水接口_1_dout16 ), .out_2(\组合逻辑_1_out_2 ));
  \_16位流水接口  \u_16位流水接口_2  (
    .Din16(\组合逻辑_1_out_2 ), .CLK(\时钟_out ), .Dout16(\n16位流水接口_2_dout16 ));  // open: 传输状态In_表明当前传输数据有效, 传输状态Out_表明当前传输数据有效, 同步清零_气泡_高电平有效, 使能端_低电平有效_stall_高电平有效
  // Probe on \n16位流水接口_2_dout16 
  \组合逻辑  \u_组合逻辑_2  (.in_1(\n16位流水接口_2_dout16 ), .out_2(\组合逻辑_2_out_2 ));
  \_16位流水接口  \u_16位流水接口_3  (
    .Din16(\组合逻辑_2_out_2 ), .CLK(\时钟_out ), .Dout16(\n16位流水接口_3_dout16 ));  // open: 传输状态In_表明当前传输数据有效, 传输状态Out_表明当前传输数据有效, 同步清零_气泡_高电平有效, 使能端_低电平有效_stall_高电平有效
  // Probe on \n16位流水接口_3_dout16 
  \组合逻辑  \u_组合逻辑_3  (.in_1(\n16位流水接口_3_dout16 ), .out_2(\组合逻辑_3_out_2 ));
  \_16位流水接口  \u_16位流水接口_4  (
    .Din16(\组合逻辑_3_out_2 ), .CLK(\时钟_out ), .Dout16(\n16位流水接口_4_dout16 ));  // open: 传输状态In_表明当前传输数据有效, 传输状态Out_表明当前传输数据有效, 同步清零_气泡_高电平有效, 使能端_低电平有效_stall_高电平有效
  // Probe on \n16位流水接口_4_dout16 

  // Notes on the sheet:
  //   计数器
  //   阶段1
  //   阶段2
  //   阶段3
  //   利用ctrl+T驱动该电路时钟，观察数据在流水线中传递的过程
  //   阶段4
  //   阶段5
endmodule

// 组合逻辑
module \组合逻辑  (
  input  [15:0] in_1,
  output [15:0] out_2
);


  assign out_2 = in_1;
endmodule

module \子电路外观测试  (
);

  wire \crc编码流水传输_1__1err , \crc编码流水传输_1__2err , \crc编码流水传输_1_clr2 , \crc编码流水传输_1_clr3 , \crc编码流水传输_1_clr4 ,
       \crc编码流水传输_1_en5 , \crc解码_1__0位错 , \crc解码_1__1位错 , \crc解码_1__2位错 , undriven_3, undriven_4, undriven_6,
       undriven_8, \偶校验检错_1_检错位 , \海明编码流水传输_1__1err , \海明编码流水传输_1__2err , \海明编码流水传输_1_clr2 ,
       \海明编码流水传输_1_clr3 , \海明编码流水传输_1_clr4 , \海明编码流水传输_1_en5 , \海明解码_1__0位错 , \海明解码_1__1位错 , \海明解码_1__2位错 ;
  wire [6:0] \国标转区位码_1_位号 , \国标转区位码_1_区号 ;
  wire [15:0] \crc解码_1_纠错后数据 , undriven, undriven_2, undriven_5, undriven_7, \偶校验检错_1_数据位 ,
       \汉字显示_1_educoder , \海明解码_1_纠错后数据 ;
  wire [16:0] \偶校验编码_1_偶校验编码 ;
  wire [21:0] \crc编码_1_crc校验码 , \海明编码_1_海明码 ;

  \国标转区位码  \u_国标转区位码_1  (.\位号 (\国标转区位码_1_位号 ), .\区号 (\国标转区位码_1_区号 ), .GB2312(undriven_2));
  \海明编码  \u_海明编码_1  (.\原始数据 (undriven), .\海明码 (\海明编码_1_海明码 ));
  \汉字显示  \u_汉字显示_1  (.EduCoder(\汉字显示_1_educoder ));
  \海明编码流水传输  \u_海明编码流水传输_1  (
    .EDU(undriven_3), .\加噪 (undriven_4), ._1err(\海明编码流水传输_1__1err ), ._2err(\海明编码流水传输_1__2err ),
    .clr2(\海明编码流水传输_1_clr2 ), .clr3(\海明编码流水传输_1_clr3 ), .clr4(\海明编码流水传输_1_clr4 ), .en5(\海明编码流水传输_1_en5 ));
  \海明解码  \u_海明解码_1  (
    .\_1位错 (\海明解码_1__1位错 ), .\_2位错 (\海明解码_1__2位错 ), .\_0位错 (\海明解码_1__0位错 ), .\海明码 (\海明编码_1_海明码 ),
    .\纠错后数据 (\海明解码_1_纠错后数据 ));
  \偶校验编码  \u_偶校验编码_1  (.\原始数据 (undriven_5), .\偶校验编码 (\偶校验编码_1_偶校验编码 ));
  \CRC编码流水传输  \crc编码流水传输_1  (
    .EDU(undriven_6), .\加噪 (undriven_8), ._1err(\crc编码流水传输_1__1err ), ._2err(\crc编码流水传输_1__2err ),
    .clr2(\crc编码流水传输_1_clr2 ), .clr3(\crc编码流水传输_1_clr3 ), .clr4(\crc编码流水传输_1_clr4 ), .en5(\crc编码流水传输_1_en5 ));
  \CRC编码  \crc编码_1  (.\原始数据 (undriven_7), .\CRC校验码 (\crc编码_1_crc校验码 ));
  \偶校验检错  \u_偶校验检错_1  (.\检错位 (\偶校验检错_1_检错位 ), .\偶校验编码 (\偶校验编码_1_偶校验编码 ), .\数据位 (\偶校验检错_1_数据位 ));
  \CRC解码  \crc解码_1  (
    .\CRC编码 (\crc编码_1_crc校验码 ), .\_1位错 (\crc解码_1__1位错 ), .\_2位错 (\crc解码_1__2位错 ), .\纠错后数据 (\crc解码_1_纠错后数据 ),
    .\_0位错 (\crc解码_1__0位错 ));

  // Notes on the sheet:
  //   GB2312
  //   国标转区位码电路封装测试
  //   原始数据
  //   GB2312
  //   EDU
  //   汉字显示电路封装测试
  //   1位错
  //   海明编码
  //   海明编解码电路封装测试
  //   加噪
  //   1err
  //   2err
  //   en5
  //   海明流水传输电路封装测试
  //   最好通过引脚悬浮提示看看连接是否正确，如果有问题，请调整封装引脚位置直至连接正确
  //   原始数据
  //   2位错
  //   0位错
  //   clr2
  //   clr3
  //   clr4
  //   原始数据
  //   EDU
  //   请勿在子电路中增删改，甚至移动引脚位置，这些都可能导致子电路外观---封装发生改变，从而使得测试电路无法正确测试
  //   提交EduCoder平台检测之前，请先检查一下对应子电路的封装连接是否正确，主要查看引脚位置是否连接正确，有否错位未连接等情况
  //   原始数据
  //   加噪
  //   1err
  //   2err
  //   en5
  //   CRC流水传输电路封装测试
  //   偶校验编码
  //   偶校验编解码电路封装测试
  //   clr2
  //   clr3
  //   clr4
  //   CRC编码
  //   CRC编解码电路封装测试
  //   检错位
  //   原始数据
  //   2位错
  //   1位错
  //   0位错
  //   原始数据
endmodule
